# Fritzing sketch Breadboard Layout (saved by Fritzing 0.9.5d)
breadboards: 1

parts:
  Part1 = InvenSense MPU6050
  Part2 = Arduino Nano (Rev3.0)
  M1 = MAX30102
  ZS-042_RTC1 = ZS-042 RTC Module
  LCD2004-I2C1 = LCD2004-I2C
  M3 = DHT11-Grove-Temperature-Sensor_1
  J1 = Piezo Speaker

nets:
  VCC: Part1.VCC, Part1.AD0, Part2.5V, M1.VIN, ZS-042_RTC1.VCC, LCD2004-I2C1.VCC, M3.connector2
  GND: Part1.GND, Part2.GND, M1.GND, ZS-042_RTC1.GND, LCD2004-I2C1.GND, M3.connector3, J1.pin1
  N1: Part1.SCL, Part2.A5, M1.SCL, ZS-042_RTC1.SCL, LCD2004-I2C1.SCL
  N2: Part1.SDA, Part2.A4, M1.SDA, ZS-042_RTC1.SDA, LCD2004-I2C1.SDA
  N3: Part2.D3, J1.pin2
  N4: Part2.D4, M3.connector0

notes:
  Arduino Nano R3
  MPU6050
  MAX30102
  DS3231
  DHT11
  Buzzer
  LCD 16x2 + I2C

custom parts:
  MAX30102: Oximeter module using the MAX30102 chip. You may wish to read (and check your module) this post on power problems with these modules: https://reedpaper.wordpress.com/2018/08/22/pulse-oximeter-max30100-max30102-how-to-fix-wrong-board/ . As usual, if you want the mounting holes in pcb, you need to drag a hole over the pad in silkscreen to actually drill the hole (by default they are not drilled)
  LCD2004-I2C: A standard character display with 4x20 characters. Comes in many colors with LCM2004 IIC attached.
